# Fritzing sketch lolin-d32-multi-point-capacitance-circuit-diagram (saved by Fritzing 0.9.4)
breadboards: 1

parts:
  U1 = Wemos Lolin D32

nets:
  N1: U1.pin_22, U1.pin_37

notes:
  foil strip

custom parts:
  Wemos Lolin D32: Based on Peter Van Epp (vanepp in forums) Wemos Lolin 32 wifi and blue tooth board based on the ESP-32 cpu
